// Digital circuit four_bit_adder.dig as structural Verilog
module four_bit_adder (
  input  [3:0] a,
  input  [3:0] b,
  input  cin,
  output cout,
  output overfl,
  output [3:0] y
);

  wire full_adder_2_cout, full_adder_3_cout, full_adder_4_cout;

  full_adder full_adder_1 (.a(a[3]), .b(b[3]), .cin(full_adder_2_cout), .sum(y[3]), .cout(cout));
  full_adder full_adder_2 (.a(a[2]), .b(b[2]), .cin(full_adder_3_cout), .sum(y[2]), .cout(full_adder_2_cout));
  full_adder full_adder_3 (.a(a[1]), .b(b[1]), .cin(full_adder_4_cout), .sum(y[1]), .cout(full_adder_3_cout));
  full_adder full_adder_4 (.a(a[0]), .b(b[0]), .cin(cin), .sum(y[0]), .cout(full_adder_4_cout));
  xor xor_1 (overfl, cout, full_adder_2_cout);

  // Other names for the same wires on the sheet: sum0 = y[0]; sum1 = y[1]; sum2 = y[2]; sum3 = y[3]
endmodule
