// Digital circuit four_bit_add_sub.dig as structural Verilog
module four_bit_add_sub (
  input  SA,
  input  SB,
  input  [3:0] a,
  input  [3:0] b,
  output [3:0] y,
  output cout,
  output ovrfl
);

  wire adder_1_p2, full_adder_1_cout, full_adder_2_cout, full_adder_3_cout, full_adder_4_cout,
       half_adder_1_sum, half_adder_2_cry, half_adder_2_sum, half_adder_3_cry, half_adder_3_sum,
       half_adder_4_cry, half_adder_4_sum, xnor_1_out, xor_1_out, xor_2_out, xor_3_out, xor_4_out, xor_5_out,
       xor_6_out, xor_7_out, xor_8_out, xor_9_out;

  xor xor_1 (xor_1_out, a[3], SA);
  xor xor_2 (xor_2_out, b[3], SB);
  xor xor_3 (xor_3_out, a[2], SA);
  xor xor_4 (xor_4_out, b[2], SB);
  xor xor_5 (xor_5_out, a[1], SA);
  xor xor_6 (xor_6_out, b[1], SB);
  xor xor_7 (xor_7_out, a[0], SA);
  xor xor_8 (xor_8_out, b[0], SB);
  xnor xnor_1 (xnor_1_out, xor_1_out, xor_2_out);
  full_adder full_adder_1 (.a(xor_1_out), .b(xor_2_out), .cin(half_adder_1_sum), .sum(y[3]), .cout(full_adder_1_cout));
  full_adder full_adder_2 (.a(xor_3_out), .b(xor_4_out), .cin(half_adder_2_sum), .sum(y[2]), .cout(full_adder_2_cout));
  full_adder full_adder_3 (.a(xor_5_out), .b(xor_6_out), .cin(half_adder_3_sum), .sum(y[1]), .cout(full_adder_3_cout));
  full_adder full_adder_4 (.a(xor_7_out), .b(xor_8_out), .cin(half_adder_4_sum), .sum(y[0]), .cout(full_adder_4_cout));
  xor xor_9 (xor_9_out, y[3], full_adder_1_cout);
  // adder adder_1: pin names not known; wires that end beside it: full_adder_1_cout, adder_1_p2, cout
  half_adder half_adder_1 (.a(full_adder_2_cout), .b(half_adder_2_cry), .sum(half_adder_1_sum), .cry(adder_1_p2));
  half_adder half_adder_2 (.a(full_adder_3_cout), .b(half_adder_3_cry), .sum(half_adder_2_sum), .cry(half_adder_2_cry));
  half_adder half_adder_3 (.a(full_adder_4_cout), .b(half_adder_4_cry), .sum(half_adder_3_sum), .cry(half_adder_3_cry));
  half_adder half_adder_4 (.a(SA), .b(SB), .sum(half_adder_4_sum), .cry(half_adder_4_cry));
  and and_1 (ovrfl, xnor_1_out, xor_9_out);
endmodule
