// Digital circuit xor_test.dig as structural Verilog
module xor_test (
  input  a,
  input  b,
  output y
);

  wire and_1_out, and_2_out, not_1_out, not_2_out;

  not not_1 (not_1_out, a);
  not not_2 (not_2_out, b);
  and and_1 (and_1_out, not_1_out, b);
  and and_2 (and_2_out, a, not_2_out);
  or or_1 (y, and_1_out, and_2_out);
endmodule
